// Logisim project control.circ as structural Verilog: 1 circuit, main circuit main
module main (
  input  start,
  input  product0,
  input  counter____31,
  input  Clock,
  output LP,
  output LMC,
  output SP_IC,
  output SM
);

  wire and_1_out, and_2_out, and_3_out, and_4_out, and_5_out, and_6_out, and_7_out, and_8_out, and_9_out,
       and_10_out, and_11_out, and_12_out, and_13_out, and_15_out, and_16_out;
  wire [2:0] N0_out, register_1_q;

  Register #(.width(3)) register_1 (.D(N0_out), .en(1'b1), .Q(register_1_q), .clk(Clock));  // open: clr
  and and_1 (and_1_out, register_1_q[2], ~register_1_q[1], ~register_1_q[0], counter____31);  // AND_Gate
  and and_2 (and_2_out, ~register_1_q[2], register_1_q[1], register_1_q[0], counter____31);  // AND_Gate
  and and_3 (and_3_out, ~register_1_q[2], register_1_q[1], ~register_1_q[0], ~product0);  // AND_Gate
  and and_4 (and_4_out, register_1_q[2], ~register_1_q[1], ~register_1_q[0], ~counter____31);  // AND_Gate
  and and_5 (and_5_out, ~register_1_q[2], register_1_q[1], register_1_q[0], ~counter____31);  // AND_Gate
  and and_6 (and_6_out, ~register_1_q[2], register_1_q[1], ~register_1_q[0], product0);  // AND_Gate
  and and_7 (and_7_out, ~register_1_q[2], ~register_1_q[1], register_1_q[0]);  // AND_Gate
  and and_8 (and_8_out, register_1_q[2], ~register_1_q[1], ~register_1_q[0], counter____31);  // AND_Gate
  and and_9 (and_9_out, ~register_1_q[2], register_1_q[1], register_1_q[0], counter____31);  // AND_Gate
  and and_10 (and_10_out, ~register_1_q[2], register_1_q[1], ~register_1_q[0], product0);  // AND_Gate
  and and_11 (and_11_out, ~register_1_q[2], ~register_1_q[1], ~register_1_q[0], start);  // AND_Gate
  or N2 (N0_out[2], and_1_out, and_2_out, and_3_out);
  or N1 (N0_out[1], and_4_out, and_5_out, and_6_out, and_7_out);
  or N0 (N0_out[0], and_8_out, and_9_out, and_10_out, and_11_out);
  and and_12 (and_12_out, register_1_q[2], ~register_1_q[1], ~register_1_q[0]);  // AND_Gate
  and and_13 (and_13_out, ~register_1_q[2], register_1_q[0]);  // AND_Gate
  and and_14 (LMC, ~register_1_q[2], ~register_1_q[1], register_1_q[0]);  // AND_Gate
  and and_15 (and_15_out, register_1_q[2], ~register_1_q[1], ~register_1_q[0]);  // AND_Gate
  and and_16 (and_16_out, ~register_1_q[2], register_1_q[1], register_1_q[0]);  // AND_Gate
  and and_17 (SM, register_1_q[2], ~register_1_q[1], ~register_1_q[0]);  // AND_Gate
  or or_1 (LP, and_12_out, and_13_out);
  or or_2 (SP_IC, and_15_out, and_16_out);
endmodule
