// Logisim project datapath.circ as structural Verilog: 1 circuit, main circuit main
module main (
  input  [31:0] Multiplier_32_Bit,
  input  [31:0] Multiplicand_32_Bit,
  input  LMC,
  input  Clock,
  input  SP_IC,
  input  LP,
  input  SM,
  output Counter____31,
  output Product0,
  output [31:0] Product_Left,
  output [31:0] Product_Right
);

  wire [4:0] counter_1_q;
  wire [31:0] adder_1_out, multiplexer_1_out, multiplexer_2_out, register_3_q, shifter_1_out, shifter_2_out;
  wire [31:1] multiplexer_3_out;
  wire [31:31] shifter_2_out_2;

  Multiplexer #(.width(32)) multiplexer_1 (
    .in0({32{1'b0}}), .in1(shifter_1_out), .out(multiplexer_1_out), .sel(SP_IC));  // open: en
  Multiplexer #(.width(32)) multiplexer_2 (
    .in0(Multiplier_32_Bit), .in1(shifter_2_out), .out(multiplexer_2_out), .sel(SP_IC));  // open: en
  Register #(.width(32)) register_1 (.D(multiplexer_1_out), .en(LP), .Q(Product_Left), .clk(Clock));  // open: clr
  Register #(.width(32)) register_2 (
    .D(multiplexer_2_out), .en(LP), .Q({Product_Right[31:1], Product0}), .clk(Clock));  // open: clr
  Register #(.width(32)) register_3 (.D(Multiplicand_32_Bit), .en(LMC), .Q(register_3_q), .clk(Clock));  // open: clr
  Multiplexer #(.width(32)) multiplexer_3 (
    .in0(adder_1_out), .in1(Product_Left), .out({multiplexer_3_out, shifter_2_out[31]}), .sel(SM));  // open: en
  Counter #(.width(5), .max('h1f)) counter_1 (
    .load(LMC), .D({5{1'b0}}), .count(SP_IC), .Q(counter_1_q), .clk(Clock));  // open: carry, clr
  Adder #(.width(32)) adder_1 (.a(register_3_q), .b(Product_Left), .out(adder_1_out));  // open: cin, cout
  Shifter #(.width(32), .shift("lr")) shifter_1 (
    .in({multiplexer_3_out, shifter_2_out[31]}), .\dist (5'b00001), .out(shifter_1_out));
  Shifter #(.width(32), .shift("lr")) shifter_2 (
    .in({Product_Right[31:1], Product0}), .\dist (5'b00001), .out({shifter_2_out_2[31], shifter_2_out[30:0]}));
  and and_1 (Counter____31, counter_1_q[0], counter_1_q[1], counter_1_q[2], counter_1_q[3], counter_1_q[4]);

  assign Product_Right[0] = Product0;

  // Notes on the sheet:
  //   Product(64 bit)
  //   Counter
endmodule
