// Logisim project mult32.circ as structural Verilog: 1 circuit, main circuit main
module main (
  input  [31:0] Multiplier,
  input  [31:0] Multiplicand,
  output [31:0] Product_left,
  output [31:0] Product_right
);

  wire clock_1_out, main_1_lmc, main_1_lp, main_1_sm, main_1_sp_ic, main_2_counter____31, main_2_product0,
       Start_out;

  Button Start (.out(Start_out));
  Clock clock_1 (.out(clock_1_out));
  control_main main_1 (
    .start(Start_out), .product0(main_2_product0), .counter____31(main_2_counter____31), .Clock(clock_1_out),
    .LP(main_1_lp), .LMC(main_1_lmc), .SP_IC(main_1_sp_ic), .SM(main_1_sm));
  datapath_main main_2 (
    .SP_IC(main_1_sp_ic), .SM(main_1_sm), .Multiplier_32_Bit(Multiplier), .Multiplicand_32_Bit(Multiplicand),
    .Product_Left(Product_left), .Product_Right(Product_right), .Counter____31(main_2_counter____31),
    .LMC(main_1_lmc), .Clock(clock_1_out), .LP(main_1_lp), .Product0(main_2_product0));

  // Notes on the sheet:
  //   Harun Albayrak - 171044014
endmodule
